# Fritzing sketch Devre Seması (saved by Fritzing 0.9.3b)
breadboards: 1

parts:
  J1 = Basic Servo
  J2 = Basic Servo
  J3 = Basic Servo
  J4 = Basic Servo
  Parça1 = Arduino Uno (Rev3)
  Parça2 = Bluetooth HC-05 Macho

nets:
  GND: J1.gnd, J2.gnd, J3.gnd, J4.gnd, Parça1.GND, Parça2.GND
  VCC: J1.vcc, J2.vcc, J3.vcc, J4.vcc, Parça1.VIN
  N1: J1.pulse, Parça1.D3_PWM
  N2: J2.pulse, Parça1.D9_PWM
  N3: J3.pulse, Parça1.D6_PWM
  N4: J4.pulse, Parça1.D5_PWM
  N5: Parça1.D10_PWM/SS, Parça2.TXD
  N6: Parça1.D11_PWM/MOSI, Parça2.RXD
  5V: Parça1.5V, Parça2.VCC
