# Fritzing sketch Devre şeması (saved by Fritzing 0.9.3b)
breadboards: 1

parts:
  Parça1 = Bluetooth HC-05 Macho
  Parça2 = Arduino Uno (Rev3)
  J1 = Basic Servo
  J2 = Basic Servo
  J3 = Basic Servo
  J4 = Basic Servo

nets:
  N1: Parça1.TXD, Parça2.D10_PWM/SS
  N2: Parça1.RXD, Parça2.D11_PWM/MOSI
  VCC: Parça1.VCC, Parça2.5V
  GND: Parça1.GND, Parça2.GND, J1.gnd, J2.gnd, J3.gnd, J4.gnd
  N3: Parça2.D9_PWM, J2.pulse
  N4: Parça2.D3_PWM, J1.pulse
  N5: Parça2.D5_PWM, J4.pulse
  N6: Parça2.D6_PWM, J3.pulse
  VCC_2: Parça2.VIN, J1.vcc, J2.vcc, J3.vcc, J4.vcc
